# Fritzing sketch Untitled_Sketch (saved by Fritzing 0.9.3b)

parts:
  Composant1 = Arduino Uno (Rev3)  # not connected
  Composant2 = Base Shield V2
  Grove_LED_Red1 = Grove LED Red
  Grove1 = Grove Buzz
  Grove_-_Bluetooth_/_BLE1 = Grove - Bluetooth / BLE
  Grove2 = Grove Infrared Receiver
  Grove3 = Grove Infrared Emitter
  Grove4 = Grove Button
  Grove5 = Grove Button
  Grove6 = Grove Button
  Grove7 = Grove Button
  U1 = 4-Channel 5v Relay Shield [package=relay-4ch5v10a]
  Grove_Ultrasonic_Ranger1 = Grove Ultrasonic Ranger

nets:
  N1: Composant2.D9, U1.IN4
  N2: Composant2.D10, U1.IN3
  N3: Composant2.D11, U1.IN2
  N4: Composant2.D12, U1.IN1
  GND: Composant2.GND, U1.GND
  5V: Composant2.5V, U1.VCC
  N5: Composant2.pin_96, Grove2.GND
  N6: Composant2.pin_97, Grove2.VCC
  N7: Composant2.pin_98, Grove2.RX
  N8: Composant2.pin_100, Grove3.GND
  N9: Composant2.pin_101, Grove3.VCC
  N10: Composant2.pin_103, Grove3.TX
  N11: Composant2.pin_104, Grove4.GND
  N12: Composant2.pin_105, Grove4.VCC
  N13: Composant2.pin_106, Grove4.NC
  N14: Composant2.pin_107, Grove4.SIG
  N15: Composant2.pin_108, Grove6.GND
  N16: Composant2.pin_109, Grove6.VCC
  N17: Composant2.pin_110, Grove6.NC
  N18: Composant2.pin_111, Grove6.SIG
  N19: Composant2.pin_116, Grove5.GND
  N20: Composant2.pin_117, Grove5.VCC
  N21: Composant2.pin_118, Grove5.NC
  N22: Composant2.pin_119, Grove5.SIG
  N23: Composant2.pin_120, Grove7.GND
  N24: Composant2.pin_121, Grove7.VCC
  N25: Composant2.pin_122, Grove7.NC
  N26: Composant2.pin_123, Grove7.SIG
  N27: Composant2.pin_140, Grove_LED_Red1.SIG
  N28: Composant2.pin_141, Grove_LED_Red1.NC1
  N29: Composant2.pin_142, Grove_LED_Red1.NC2
  N30: Composant2.pin_143, Grove_LED_Red1.GND
  N31: Composant2.pin_144, Grove1.SIG
  N32: Composant2.pin_146, Grove1.VCC
  N33: Composant2.pin_147, Grove1.GND
  N34: Composant2.pin_148, Grove_Ultrasonic_Ranger1.SIG
  N35: Composant2.pin_149, Grove_Ultrasonic_Ranger1.NC
  N36: Composant2.pin_150, Grove_Ultrasonic_Ranger1.VCC
  N37: Composant2.pin_151, Grove_Ultrasonic_Ranger1.GND
  N38: Composant2.pin_152, Grove_-_Bluetooth_/_BLE1.Rx
  N39: Composant2.pin_153, Grove_-_Bluetooth_/_BLE1.Tx
  N40: Composant2.pin_154, Grove_-_Bluetooth_/_BLE1.VCC
  N41: Composant2.pin_155, Grove_-_Bluetooth_/_BLE1.GND

custom parts:
  Grove LED Red: LED red, Grove connector.
  4-Channel 5v Relay Shield: 4 Channel 5v Relay Shield w. 2x SPD-06VDC-SD-C
  Grove Ultrasonic Ranger: Ultrasonic Ranger, Grove connector.
